// Logisim project CPU - single core error - no mem error.circ as structural Verilog: 7 circuits, main circuit main
module main (
  input  RESET,
  output [15:0] ACC_CONTROL,
  output [24:0] out_3,
  output [15:0] CACHE_CTRL,
  output [24:0] out_5,
  output [15:0] ACC_CONTROL_2,
  output [15:0] CACHE_CTRL_2
);

  wire clock_1_out, cmu_1_mvenable;
  wire [11:0] cmu_1_mv_adds;
  wire [15:0] cmu_1_im0adds, cmu_1_im1adds, cmu_1_mv_data, core_1_add, core_2_add;
  wire [24:0] cmu_1_core0data, cmu_1_core1data;

  Clock clock_1 (.out(clock_1_out));
  Core core_1 (
    .mvAdds(cmu_1_mv_adds), .Add(core_1_add), .Data(cmu_1_core0data), .ResCTRLLog(RESET),
    .mvEnable(cmu_1_mvenable), .CLK(clock_1_out), .mvData(cmu_1_mv_data), .CACHE_CTRL(CACHE_CTRL),
    .acc_ctrl(ACC_CONTROL));
  Core core_2 (
    .mvAdds(cmu_1_mv_adds), .Add(core_2_add), .Data(cmu_1_core1data), .ResCTRLLog(RESET),
    .mvEnable(cmu_1_mvenable), .CLK(clock_1_out), .mvData(cmu_1_mv_data), .CACHE_CTRL(CACHE_CTRL_2),
    .acc_ctrl(ACC_CONTROL_2));
  CMU cmu_1 (
    .core0adds(core_1_add), .core1adds(core_2_add), .core0data(cmu_1_core0data), .core1data(cmu_1_core1data),
    .im0adds(cmu_1_im0adds), .im1adds(cmu_1_im1adds), .mv_adds(cmu_1_mv_adds), .im0data(out_3),
    .mvEnable(cmu_1_mvenable), .mv_DATA(cmu_1_mv_data), .im1data(out_5));
  ROM #(.addrWidth(16), .dataWidth(25)) rom_1 (.addr(cmu_1_im0adds), .data(out_3), .sel(1'b1));
  ROM #(.addrWidth(16), .dataWidth(25)) rom_2 (.addr(cmu_1_im1adds), .data(out_5), .sel(1'b1));

  // Notes on the sheet:
  //   contents of rom_1 (hex, n*v repeats v):
  //   4000 2003 9000 4001
  //   contents of rom_2 (hex, n*v repeats v):
  //   2002 4000 2004 9000 4001 1001002
endmodule

module ALU (
  input  [15:0] A,
  input  [15:0] B,
  input  [3:0] sALU,
  output [15:0] out_4
);

  wire [15:0] adder_1_out, and_1_out, divider_1_out, multiplier_1_out, negator_1_out, not_1_out, or_1_out,
       shifter_1_out, shifter_2_out, subtractor_1_out, xor_1_out;

  assign not_1_out = ~A;  // NOT_Gate not_1, 16 bits wide
  Shifter #(.width(16), .shift("lr")) shifter_1 (.in(A), .\dist (B[3:0]), .out(shifter_1_out));
  Shifter #(.width(16)) shifter_2 (.in(A), .\dist (B[3:0]), .out(shifter_2_out));
  Adder #(.width(16)) adder_1 (.a(A), .b(B), .out(adder_1_out));  // open: cin, cout
  Subtractor #(.width(16)) subtractor_1 (.a(A), .b(B), .out(subtractor_1_out));  // open: bin, bout
  assign xor_1_out = A ^ B;  // XOR_Gate xor_1, 16 bits wide
  assign and_1_out = A & B;  // AND_Gate and_1, 16 bits wide
  assign or_1_out = A | B;  // OR_Gate or_1, 16 bits wide
  Multiplier #(.width(16)) multiplier_1 (.a(A), .b(B), .out(multiplier_1_out));  // open: cin, cout
  Divider #(.width(16)) divider_1 (.a(A), .b(B), .out(divider_1_out));  // open: upper, rem
  Negator #(.width(16)) negator_1 (.in(A), .out(negator_1_out));
  Multiplexer #(.select(4), .width(16), .enable("false")) multiplexer_1 (
    .in1(xor_1_out), .in2(and_1_out), .in3(not_1_out), .in4(or_1_out), .in5(multiplier_1_out),
    .in6(negator_1_out), .in7(shifter_1_out), .in8(shifter_2_out), .in9(adder_1_out), .in10(divider_1_out),
    .in11(subtractor_1_out), .out(out_4), .sel(sALU));  // open: in0, in12, in13, in14, in15
endmodule

module Core (
  input  mvEnable,
  input  [15:0] mvData,
  input  [11:0] mvAdds,
  input  CLK,
  input  ResCTRLLog,
  input  [24:0] Data,
  output [15:0] CACHE_CTRL,
  output [15:0] acc_ctrl,
  output [15:0] Add
);

  wire and_1_out, comparator_1_eq, comparator_1_lt, ff7controledition_1_dw1, ff7controledition_1_dw4,
       ff7controledition_1_ld, ff7controledition_1_sel, ff7controledition_1_up1, multiplexer_6_out,
       not_1_out, not_2_out, or_1_out;
  wire [1:0] ff7controledition_1_dw2_1;
  wire [3:0] ff7controledition_1_salu4;
  wire [11:0] multiplexer_2_out;
  wire [15:0] adder_1_out, adder_2_out, alu_1_out_4, bit_extender_1_out, multiplexer_1_out,
       multiplexer_3_out, ram_1_data;

  ff7Controledition ff7controledition_1 (
    .OP0(Data[15]), .OP1(Data[14]), .OP2(Data[13]), .OP3(Data[12]), .sALU1(ff7controledition_1_salu4[3]),
    .sALU2(ff7controledition_1_salu4[2]), .sALU3(ff7controledition_1_salu4[1]),
    .sALU4(ff7controledition_1_salu4[0]), .dw1(ff7controledition_1_dw1), .dw2(ff7controledition_1_dw2_1[1]),
    .dw2_1(ff7controledition_1_dw2_1[0]), .dw4(ff7controledition_1_dw4), .up1(ff7controledition_1_up1),
    .LD(ff7controledition_1_ld), .Sel(ff7controledition_1_sel));
  Adder #(.width(16)) adder_1 (.a(Add), .b(bit_extender_1_out), .out(adder_1_out));  // open: cin, cout
  Adder #(.width(16)) adder_2 (.a(Add), .b(16'h1), .out(adder_2_out));  // open: cin, cout
  Multiplexer #(.width(16), .enable("false")) multiplexer_1 (
    .in0(adder_1_out), .in1(adder_2_out), .out(multiplexer_1_out), .sel(not_1_out));
  not not_1 (not_1_out, multiplexer_6_out);
  Register #(.width(16)) PROG_COUNT (.D(multiplexer_1_out), .Q(Add), .clk(CLK), .clr(ResCTRLLog));  // open: en
  Multiplexer #(.width(12), .enable("false")) multiplexer_2 (
    .in0(Data[11:0]), .in1(mvAdds), .out(multiplexer_2_out), .sel(mvEnable));
  or or_1 (or_1_out, mvEnable, ff7controledition_1_sel);
  and and_1 (and_1_out, ff7controledition_1_ld, not_2_out);
  not not_2 (not_2_out, mvEnable);
  assign bit_extender_1_out = {{4{Data[11]}}, Data[11:0]};  // Bit_Extender bit_extender_1
  RAM #(.addrWidth(12), .dataWidth(16)) ram_1 (
    .addr(multiplexer_2_out), .data(ram_1_data), .sel(or_1_out), .clk(CLK), .ld(and_1_out), .clr(ResCTRLLog));
  Register #(.width(16)) ACC (
    .D(multiplexer_3_out), .en(ff7controledition_1_dw4), .Q(acc_ctrl), .clk(CLK), .clr(ResCTRLLog));
  Multiplexer #(.select(2), .width(16), .enable("false")) multiplexer_3 (
    .in0(ram_1_data), .in1(bit_extender_1_out), .in2(alu_1_out_4), .in3(ram_1_data), .out(multiplexer_3_out),
    .sel(ff7controledition_1_dw2_1));
  Multiplexer #(.width(16), .enable("false")) multiplexer_4 (
    .in1(mvData), .out(CACHE_CTRL), .sel(mvEnable));  // open: in0
  Comparator #(.width(16)) comparator_1 (
    .a(acc_ctrl), .b({16{1'b0}}), .eq(comparator_1_eq), .lt(comparator_1_lt));  // open: gt
  Multiplexer #(.width(16), .enable("false")) multiplexer_5 (
    .in1(acc_ctrl), .out(ram_1_data), .sel(ff7controledition_1_dw1));  // open: in0
  Multiplexer #(.enable("false")) multiplexer_6 (
    .in0(comparator_1_eq), .in1(comparator_1_lt), .out(multiplexer_6_out), .sel(ff7controledition_1_up1));
  ALU alu_1 (.A(acc_ctrl), .B(ram_1_data), .sALU(ff7controledition_1_salu4), .out_4(alu_1_out_4));

  // Notes on the sheet:
  //   Sel
  //   LD
  //   dw2
  //   dw2_1
  //   dw4
  //   up1
  //   dw1//str
endmodule

module CMU (
  input  [15:0] core0adds,
  input  [15:0] core1adds,
  input  [24:0] im0data,
  input  [24:0] im1data,
  output [15:0] im0adds,
  output [15:0] im1adds,
  output [11:0] mv_adds,
  output [24:0] core0data,
  output mvEnable,
  output [15:0] mv_DATA,
  output [24:0] core1data
);

  wire move_sel, undriven;

  mvControl move (.mv0(im0data[24]), .mv1(im1data[24]), .sel(move_sel), .enb(mvEnable));
  Multiplexer #(.width(12)) multiplexer_1 (
    .in0(core0adds[11:0]), .in1(core1adds[11:0]), .out(mv_adds), .sel(move_sel), .en(undriven));
  Multiplexer #(.width(16)) multiplexer_2 (
    .in0(im0data[15:0]), .in1(im1data[15:0]), .out(mv_DATA), .sel(move_sel), .en(undriven));

  assign core0data = im0data;
  assign core1data = im1data;
  assign im0adds = core0adds;
  assign im1adds = core1adds;
endmodule

module ff7Controledition (
  input  OP0,
  input  OP1,
  input  OP2,
  input  OP3,
  output sALU1,
  output sALU2,
  output sALU3,
  output sALU4,
  output dw1,
  output dw2,
  output dw2_1,
  output dw4,
  output up1,
  output LD,
  output Sel
);

  wire and_1_out, and_2_out, and_3_out, and_4_out, and_5_out, and_6_out, and_7_out, and_8_out, and_9_out,
       and_10_out, and_11_out, and_12_out, and_13_out, and_14_out, and_15_out, and_16_out, and_17_out,
       and_19_out, not_1_out, not_2_out, not_3_out, not_4_out, not_5_out, not_6_out, not_7_out, not_8_out,
       not_9_out, not_10_out, not_11_out, not_12_out, not_13_out, not_14_out, not_15_out, not_16_out,
       not_17_out, not_18_out, not_19_out, not_20_out, not_21_out, not_22_out, not_23_out, not_24_out,
       not_25_out, not_26_out;

  not not_1 (not_1_out, OP1);
  not not_2 (not_2_out, OP2);
  and and_1 (and_1_out, not_1_out, not_2_out, OP3);
  not not_3 (not_3_out, OP1);
  and and_2 (and_2_out, not_3_out, OP2, not_4_out);
  not not_4 (not_4_out, OP3);
  and and_3 (and_3_out, OP0, OP1, not_5_out);
  not not_5 (not_5_out, OP3);
  not not_6 (not_6_out, OP1);
  not not_7 (not_7_out, OP2);
  and and_4 (and_4_out, not_6_out, not_7_out, not_8_out);
  not not_8 (not_8_out, OP3);
  not not_9 (not_9_out, OP1);
  and and_5 (and_5_out, not_9_out, OP2, OP3);
  and and_6 (and_6_out, OP0, OP1, OP3);
  not not_10 (not_10_out, OP0);
  and and_7 (and_7_out, not_10_out, OP2);
  not not_11 (not_11_out, OP1);
  and and_8 (and_8_out, not_11_out, OP2, not_12_out);
  not not_12 (not_12_out, OP3);
  and and_9 (and_9_out, OP0, OP1, not_13_out);
  not not_13 (not_13_out, OP2);
  and and_10 (and_10_out, OP0, OP1, OP3);
  not not_14 (not_14_out, OP0);
  and and_11 (and_11_out, not_14_out, not_15_out);
  not not_15 (not_15_out, OP2);
  not not_16 (not_16_out, OP0);
  and and_12 (and_12_out, not_16_out, not_17_out);
  not not_17 (not_17_out, OP3);
  not not_18 (not_18_out, OP1);
  and and_13 (and_13_out, not_18_out, OP3);
  not not_19 (not_19_out, OP1);
  and and_14 (and_14_out, not_19_out, OP2);
  and and_15 (and_15_out, OP0, OP2, OP3);
  not not_20 (not_20_out, OP0);
  and and_16 (and_16_out, not_20_out, not_21_out);
  not not_21 (not_21_out, OP1);
  not not_22 (not_22_out, OP0);
  not not_23 (not_23_out, OP2);
  and and_17 (and_17_out, not_22_out, not_23_out, not_24_out);
  not not_24 (not_24_out, OP3);
  or or_1 (dw2, OP3, OP1, OP0);
  not not_25 (not_25_out, OP0);
  and and_18 (dw2_1, not_25_out, not_26_out);
  not not_26 (not_26_out, OP1);
  and and_19 (and_19_out, OP1, OP3);
  or or_2 (LD, OP3, OP2, OP0);
  or or_3 (sALU1, and_1_out, and_2_out, and_3_out);
  or or_4 (sALU2, and_4_out, and_5_out, and_6_out);
  or or_5 (sALU3, and_7_out, and_8_out, and_9_out, and_10_out);
  or or_6 (sALU4, and_11_out, and_12_out, and_13_out, and_14_out, and_15_out);
  or or_7 (dw1, and_16_out, and_17_out);
  or or_8 (dw4, OP2, and_19_out, OP0);

  assign Sel = 1'b1;
  assign up1 = OP3;
endmodule

// MV
module mvControl (
  input  mv0,
  input  mv1,
  output sel,
  output enb
);

  wire and_1_out, and_2_out, not_1_out, not_2_out;

  not not_1 (not_1_out, mv0);
  not not_2 (not_2_out, mv1);
  and and_1 (and_1_out, not_1_out, mv1);
  and and_2 (and_2_out, mv0, not_2_out);
  or or_1 (enb, and_1_out, and_2_out);

  assign sel = mv1;
endmodule

module control (
  input  OP0,
  input  OP1,
  input  OP2,
  input  OP3,
  output sALU1,
  output sALU2,
  output sALU3,
  output sALU4,
  output dw1,
  output dw2,
  output dw2_1,
  output dw4,
  output up1,
  output up1_1,
  output LD,
  output Sel
);

  wire and_1_out, and_2_out, and_3_out, and_4_out, and_5_out, and_6_out, and_7_out, and_8_out, and_9_out,
       and_10_out, and_11_out, and_12_out, and_13_out, and_14_out, and_15_out, and_17_out, not_1_out,
       not_2_out, not_3_out, not_4_out, not_5_out, not_6_out, not_7_out, not_8_out, not_9_out, not_10_out,
       not_11_out, not_12_out, not_13_out, not_14_out, not_15_out, not_16_out, not_17_out, not_18_out,
       not_19_out, not_20_out, not_21_out, not_22_out, not_23_out, not_24_out, not_25_out, not_26_out,
       not_27_out, not_28_out, not_29_out;

  not not_1 (not_1_out, OP1);
  not not_2 (not_2_out, OP2);
  and and_1 (and_1_out, not_1_out, not_2_out, OP3);
  not not_3 (not_3_out, OP1);
  and and_2 (and_2_out, not_3_out, OP2, not_4_out);
  not not_4 (not_4_out, OP3);
  and and_3 (and_3_out, OP0, OP1, not_5_out);
  not not_5 (not_5_out, OP3);
  not not_6 (not_6_out, OP1);
  and and_4 (and_4_out, not_6_out, not_7_out, not_8_out);
  not not_7 (not_7_out, OP2);
  not not_8 (not_8_out, OP3);
  not not_9 (not_9_out, OP1);
  and and_5 (and_5_out, not_9_out, OP2, OP3);
  and and_6 (and_6_out, OP0, OP1, OP3);
  not not_10 (not_10_out, OP0);
  and and_7 (and_7_out, not_10_out, OP2);
  not not_11 (not_11_out, OP1);
  and and_8 (and_8_out, not_11_out, OP2, not_12_out);
  not not_12 (not_12_out, OP3);
  and and_9 (and_9_out, OP0, OP1, not_13_out);
  not not_13 (not_13_out, OP2);
  and and_10 (and_10_out, OP0, OP1, OP3);
  not not_14 (not_14_out, OP0);
  and and_11 (and_11_out, not_14_out, not_15_out);
  not not_15 (not_15_out, OP2);
  not not_16 (not_16_out, OP0);
  and and_12 (and_12_out, not_16_out, not_17_out);
  not not_17 (not_17_out, OP3);
  not not_18 (not_18_out, OP1);
  and and_13 (and_13_out, not_18_out, OP3);
  not not_19 (not_19_out, OP1);
  and and_14 (and_14_out, not_19_out, OP2);
  and and_15 (and_15_out, OP0, OP2, OP3);
  not not_20 (not_20_out, OP0);
  not not_21 (not_21_out, OP1);
  or or_1 (dw2, OP3, OP1, OP0);
  not not_22 (not_22_out, OP0);
  and and_16 (dw2_1, not_22_out, not_23_out);
  not not_23 (not_23_out, OP1);
  and and_17 (and_17_out, OP1, OP3);
  not not_24 (not_24_out, OP0);
  and and_18 (up1_1, not_24_out, not_25_out, not_26_out);
  not not_25 (not_25_out, OP1);
  not not_26 (not_26_out, OP2);
  not not_27 (not_27_out, OP0);
  and and_19 (LD, not_27_out, not_28_out, not_29_out);
  not not_28 (not_28_out, OP2);
  not not_29 (not_29_out, OP3);
  or or_2 (Sel, OP3, OP2, OP0);
  or or_3 (sALU1, and_1_out, and_2_out, and_3_out);
  or or_4 (sALU2, and_4_out, and_5_out, and_6_out);
  or or_5 (sALU3, and_7_out, and_8_out, and_9_out, and_10_out);
  or or_6 (sALU4, and_11_out, and_12_out, and_13_out, and_14_out, and_15_out);
  and and_20 (dw1, not_20_out, not_21_out, OP2, OP3);
  or or_7 (dw4, OP2, and_17_out, OP0);

  assign up1 = OP3;
endmodule
